// Logisim project CpuEmulator.circ as structural Verilog: 1 circuit, main circuit main
module main (
  input  [15:0] in_1,
  input  [3:0] in_2,
  input  [15:0] in_3,
  input  [15:0] in_4,
  input  [3:0] in_5,
  input  [3:0] in_6,
  input  [3:0] in_7,
  input  [3:0] in_8,
  input  [3:0] in_9,
  input  [3:0] in_10,
  input  [3:0] in_11,
  input  [15:0] in_12,
  input  in_13,
  input  in_14,
  input  [3:0] in_15,
  input  [3:0] in_16,
  input  [3:0] in_17,
  input  [3:0] in_18,
  input  [3:0] in_19,
  input  [3:0] in_20,
  input  [3:0] in_21,
  input  [3:0] in_22,
  input  [3:0] in_23,
  input  [3:0] in_24
);

  wire and_1_out, and_2_out, and_3_out, and_4_out, and_5_out, and_6_out, and_7_out, and_8_out, and_9_out,
       and_10_out, and_11_out, and_12_out, and_13_out, and_14_out, and_15_out, and_16_out, clock_1_out,
       clock_2_out, comparator_1_gt, comparator_2_eq, comparator_3_eq, comparator_3_gt, comparator_4_lt,
       comparator_5_lt, comparator_6_eq, comparator_7_eq, comparator_8_eq, comparator_9_lt, comparator_10_eq,
       comparator_11_eq, comparator_12_eq, comparator_13_lt, comparator_14_lt, decoder_1_out0,
       decoder_1_out1, decoder_1_out2, decoder_1_out3, decoder_1_out4, decoder_1_out5, decoder_1_out6,
       decoder_1_out7, decoder_1_out8, decoder_1_out9, decoder_1_out10, decoder_1_out11, decoder_1_out12,
       decoder_1_out13, decoder_1_out14, decoder_1_out15, not_1_out, or_1_out, or_2_out, subtractor_1_bout;
  wire [1:0] multiplexer_18_out;
  wire [3:0] multiplexer_2_out, multiplexer_10_out, multiplexer_12_out, multiplexer_16_out,
       multiplexer_17_out, subtractor_1_out, subtractor_4_out;
  wire [3:2] multiplexer_18_out_2;
  wire [15:0] adder_1_out, adder_2_out, adder_3_out, adder_4_out, adder_5_out, adder_6_out,
       bit_extender_1_out, bit_extender_2_out, bit_extender_3_out, bit_extender_4_out, divider_1_out,
       divider_2_out, multiplexer_1_out, multiplexer_3_out, multiplexer_4_out, multiplexer_5_out,
       multiplexer_6_out, multiplexer_7_out, multiplexer_8_out, multiplexer_9_out, multiplexer_11_out,
       multiplexer_13_out, multiplexer_14_out, multiplexer_15_out, multiplier_1_out, multiplier_2_out,
       negator_1_out, negator_2_out, PC_q, ram_1_dout, ram_2_dout, register_1_q, register_2_q, register_3_q,
       register_4_q, register_5_q, register_6_q, register_7_q, register_8_q, register_9_q, register_10_q,
       register_11_q, register_12_q, register_13_q, register_14_q, register_15_q, register_16_q,
       subtractor_2_out, subtractor_3_out, subtractor_5_out, subtractor_6_out;

  Comparator #(.mode("unsigned"), .width(4)) comparator_1 (
    .a(ram_1_dout[15:12]), .b(in_21), .gt(comparator_1_gt));  // open: eq, lt
  Comparator #(.mode("unsigned"), .width(4)) comparator_2 (
    .a(in_22), .b(ram_1_dout[15:12]), .eq(comparator_2_eq));  // open: gt, lt
  Decoder #(.enable("false"), .select(4)) decoder_1 (
    .out0(decoder_1_out0), .out1(decoder_1_out1), .out2(decoder_1_out2), .out3(decoder_1_out3),
    .out4(decoder_1_out4), .out5(decoder_1_out5), .out6(decoder_1_out6), .out7(decoder_1_out7),
    .out8(decoder_1_out8), .out9(decoder_1_out9), .out10(decoder_1_out10), .out11(decoder_1_out11),
    .out12(decoder_1_out12), .out13(decoder_1_out13), .out14(decoder_1_out14), .out15(decoder_1_out15),
    .sel(ram_1_dout[11:8]));
  or or_1 (or_1_out, comparator_1_gt, comparator_2_eq);
  not not_1 (not_1_out, or_1_out);
  Register #(.width(16)) PC (.D(multiplexer_13_out), .en(in_13), .clk(clock_1_out), .Q(PC_q));  // open: clr
  Clock #(.highDuration(2), .lowDuration(2)) clock_1 (.out(clock_1_out));
  and and_1 (and_1_out, not_1_out, decoder_1_out0);
  and and_2 (and_2_out, not_1_out, decoder_1_out1);
  and and_3 (and_3_out, not_1_out, decoder_1_out2);
  and and_4 (and_4_out, not_1_out, decoder_1_out3);
  and and_5 (and_5_out, not_1_out, decoder_1_out4);
  and and_6 (and_6_out, not_1_out, decoder_1_out5);
  and and_7 (and_7_out, not_1_out, decoder_1_out6);
  and and_8 (and_8_out, not_1_out, decoder_1_out7);
  and and_9 (and_9_out, not_1_out, decoder_1_out8);
  and and_10 (and_10_out, not_1_out, decoder_1_out9);
  and and_11 (and_11_out, not_1_out, decoder_1_out10);
  and and_12 (and_12_out, not_1_out, decoder_1_out11);
  and and_13 (and_13_out, not_1_out, decoder_1_out12);
  and and_14 (and_14_out, not_1_out, decoder_1_out13);
  and and_15 (and_15_out, not_1_out, decoder_1_out14);
  and and_16 (and_16_out, not_1_out, decoder_1_out15);
  assign bit_extender_1_out = {{8{ram_1_dout[7]}}, ram_1_dout[7:0]};  // Bit_Extender bit_extender_1
  assign bit_extender_2_out = {{4{ram_1_dout[11]}}, ram_1_dout[11:0]};  // Bit_Extender bit_extender_2
  Register #(.width(16)) register_1 (
    .D(multiplexer_1_out), .en(and_1_out), .clk(clock_1_out), .Q(register_1_q));  // open: clr
  Register #(.width(16)) register_2 (
    .D(multiplexer_1_out), .en(and_2_out), .clk(clock_1_out), .Q(register_2_q));  // open: clr
  Register #(.width(16)) register_3 (
    .D(multiplexer_1_out), .en(and_3_out), .clk(clock_1_out), .Q(register_3_q));  // open: clr
  Register #(.width(16)) register_4 (
    .D(multiplexer_1_out), .en(and_4_out), .clk(clock_1_out), .Q(register_4_q));  // open: clr
  Register #(.width(16)) register_5 (
    .D(multiplexer_1_out), .en(and_5_out), .clk(clock_1_out), .Q(register_5_q));  // open: clr
  Register #(.width(16)) register_6 (
    .D(multiplexer_1_out), .en(and_6_out), .clk(clock_1_out), .Q(register_6_q));  // open: clr
  Register #(.width(16)) register_7 (
    .D(multiplexer_1_out), .en(and_7_out), .clk(clock_1_out), .Q(register_7_q));  // open: clr
  Register #(.width(16)) register_8 (
    .D(multiplexer_1_out), .en(and_8_out), .clk(clock_1_out), .Q(register_8_q));  // open: clr
  Register #(.width(16)) register_9 (
    .D(multiplexer_1_out), .en(and_9_out), .clk(clock_1_out), .Q(register_9_q));  // open: clr
  Register #(.width(16)) register_10 (
    .D(multiplexer_1_out), .en(and_10_out), .clk(clock_1_out), .Q(register_10_q));  // open: clr
  Register #(.width(16)) register_11 (
    .D(multiplexer_1_out), .en(and_11_out), .clk(clock_1_out), .Q(register_11_q));  // open: clr
  Register #(.width(16)) register_12 (
    .D(multiplexer_1_out), .en(and_12_out), .clk(clock_1_out), .Q(register_12_q));  // open: clr
  Register #(.width(16)) register_13 (
    .D(multiplexer_1_out), .en(and_13_out), .clk(clock_1_out), .Q(register_13_q));  // open: clr
  Register #(.width(16)) register_14 (
    .D(multiplexer_1_out), .en(and_14_out), .clk(clock_1_out), .Q(register_14_q));  // open: clr
  Register #(.width(16)) register_15 (
    .D(multiplexer_1_out), .en(and_15_out), .clk(clock_1_out), .Q(register_15_q));  // open: clr
  Register #(.width(16)) register_16 (
    .D(multiplexer_1_out), .en(and_16_out), .clk(clock_1_out), .Q(register_16_q));  // open: clr
  Multiplexer #(.select(2), .width(16)) multiplexer_1 (
    .in0(multiplexer_15_out), .in1(multiplexer_6_out), .in2(multiplexer_5_out), .in3(ram_2_dout),
    .out(multiplexer_1_out), .sel(multiplexer_2_out[1:0]));
  Subtractor #(.width(4)) subtractor_1 (
    .a(ram_1_dout[15:12]), .b(in_23), .out(subtractor_1_out), .bout(subtractor_1_bout));  // open: bin
  Multiplexer #(.width(4)) multiplexer_2 (
    .in0(subtractor_1_out), .in1(in_24), .out(multiplexer_2_out), .sel(subtractor_1_bout));
  Adder #(.width(16)) adder_1 (.a(PC_q), .b(bit_extender_1_out), .out(adder_1_out));  // open: cin, cout
  Subtractor #(.width(16)) subtractor_2 (.a(PC_q), .b(negator_1_out), .out(subtractor_2_out));  // open: bin, bout
  Negator #(.width(16)) negator_1 (.in(bit_extender_1_out), .out(negator_1_out));
  Adder #(.width(16)) adder_2 (.a(PC_q), .b(bit_extender_2_out), .out(adder_2_out));  // open: cin, cout
  Subtractor #(.width(16)) subtractor_3 (.a(PC_q), .b(negator_2_out), .out(subtractor_3_out));  // open: bin, bout
  Negator #(.width(16)) negator_2 (.in(bit_extender_2_out), .out(negator_2_out));
  Adder #(.width(16)) adder_3 (.a(in_12), .b(PC_q), .out(adder_3_out));  // open: cin, cout
  RAM #(.addrWidth(16), .dataWidth(16), .enables("line")) ram_1 (
    .addr(PC_q), .we(in_14), .clk(clock_1_out), .dout(ram_1_dout));  // open: din
  Multiplexer #(.width(16)) multiplexer_3 (
    .in0(adder_1_out), .in1(subtractor_2_out), .out(multiplexer_3_out), .sel(comparator_4_lt));
  Multiplexer #(.width(16)) multiplexer_4 (
    .in0(adder_2_out), .in1(subtractor_3_out), .out(multiplexer_4_out), .sel(comparator_5_lt));
  Multiplexer #(.width(16)) multiplexer_5 (
    .in0(multiplexer_6_out), .in1(bit_extender_3_out), .out(multiplexer_5_out), .sel(comparator_6_eq));
  Comparator #(.mode("unsigned"), .width(16)) comparator_3 (
    .a(multiplexer_6_out), .b(in_1), .gt(comparator_3_gt), .eq(comparator_3_eq));  // open: lt
  Comparator #(.width(16)) comparator_4 (.a(bit_extender_1_out), .b(in_3), .lt(comparator_4_lt));  // open: gt, eq
  Comparator #(.width(16)) comparator_5 (.a(bit_extender_2_out), .b(in_4), .lt(comparator_5_lt));  // open: gt, eq
  Comparator #(.width(4)) comparator_6 (.a(ram_1_dout[15:12]), .b(in_19), .eq(comparator_6_eq));  // open: gt, lt
  Multiplexer #(.select(4), .width(16)) multiplexer_6 (
    .in0(register_1_q), .in1(register_2_q), .in2(register_3_q), .in3(register_4_q), .in4(register_5_q),
    .in5(register_6_q), .in6(register_7_q), .in7(register_8_q), .in8(register_9_q), .in9(register_10_q),
    .in10(register_11_q), .in11(register_12_q), .in12(register_13_q), .in13(register_14_q),
    .in14(register_15_q), .in15(register_16_q), .out(multiplexer_6_out), .sel(multiplexer_12_out));
  Multiplexer #(.select(4), .width(16)) multiplexer_7 (
    .in0(register_1_q), .in1(register_2_q), .in2(register_3_q), .in3(register_4_q), .in4(register_5_q),
    .in5(register_6_q), .in6(register_7_q), .in7(register_8_q), .in8(register_9_q), .in9(register_10_q),
    .in10(register_11_q), .in11(register_12_q), .in12(register_13_q), .in13(register_14_q),
    .in14(register_15_q), .in15(register_16_q), .out(multiplexer_7_out), .sel(multiplexer_10_out));
  Comparator #(.mode("unsigned"), .width(4)) comparator_7 (
    .a(ram_1_dout[15:12]), .b(in_2), .eq(comparator_7_eq));  // open: gt, lt
  Multiplexer #(.width(16)) multiplexer_8 (
    .in0(adder_3_out), .in1(multiplexer_3_out), .out(multiplexer_8_out), .sel(comparator_3_gt));
  Multiplexer #(.width(16)) multiplexer_9 (
    .in0(adder_3_out), .in1(multiplexer_3_out), .out(multiplexer_9_out), .sel(comparator_3_eq));
  assign bit_extender_3_out = {{8{1'b0}}, ram_1_dout[7:0]};  // Bit_Extender bit_extender_3
  Multiplexer #(.width(4)) multiplexer_10 (
    .in0(ram_1_dout[3:0]), .in1(ram_1_dout[7:4]), .out(multiplexer_10_out), .sel(or_2_out));
  assign bit_extender_4_out = {{12{1'b0}}, ram_1_dout[3:0]};  // Bit_Extender bit_extender_4
  Multiplexer #(.width(16)) multiplexer_11 (
    .in0(multiplexer_9_out), .in1(multiplexer_8_out), .out(multiplexer_11_out), .sel(comparator_7_eq));
  Multiplexer #(.width(4)) multiplexer_12 (
    .in0(ram_1_dout[7:4]), .in1(ram_1_dout[11:8]), .out(multiplexer_12_out), .sel(or_2_out));
  RAM #(.addrWidth(16), .dataWidth(16), .enables("line")) ram_2 (
    .addr(adder_6_out), .we(comparator_12_eq), .clk(clock_2_out), .din(multiplexer_6_out), .dout(ram_2_dout));
  Clock clock_2 (.out(clock_2_out));
  Multiplexer #(.select(2), .width(16)) multiplexer_13 (
    .in0(PC_q), .in1(adder_3_out), .in2(multiplexer_4_out), .in3(multiplexer_11_out),
    .out(multiplexer_13_out), .sel(multiplexer_18_out));
  Comparator #(.mode("unsigned"), .width(4)) comparator_8 (
    .a(ram_1_dout[15:12]), .b(in_17), .eq(comparator_8_eq));  // open: gt, lt
  Subtractor #(.width(4)) subtractor_4 (.a(ram_1_dout[15:12]), .b(in_18), .out(subtractor_4_out));  // open: bin, bout
  Adder #(.width(16)) adder_4 (.a(multiplexer_6_out), .b(multiplexer_7_out), .out(adder_4_out));  // open: cin, cout
  Adder #(.width(16)) adder_5 (.a(multiplexer_6_out), .b(bit_extender_4_out), .out(adder_5_out));  // open: cin, cout
  Subtractor #(.width(16)) subtractor_5 (
    .a(multiplexer_6_out), .b(multiplexer_7_out), .out(subtractor_5_out));  // open: bin, bout
  Subtractor #(.width(16)) subtractor_6 (
    .a(multiplexer_6_out), .b(bit_extender_4_out), .out(subtractor_6_out));  // open: bin, bout
  Multiplier #(.mode("twosComplement"), .width(16)) multiplier_1 (
    .a(multiplexer_6_out), .b(multiplexer_7_out), .out(multiplier_1_out));  // open: cin, cout
  Multiplier #(.mode("twosComplement"), .width(16)) multiplier_2 (
    .a(multiplexer_6_out), .b(bit_extender_4_out), .out(multiplier_2_out));  // open: cin, cout
  Divider #(.mode("twosComplement"), .width(16)) divider_1 (
    .a(multiplexer_6_out), .b(multiplexer_7_out), .out(divider_1_out));  // open: upper, rem
  Divider #(.mode("twosComplement"), .width(16)) divider_2 (
    .a(multiplexer_6_out), .b(bit_extender_4_out), .out(divider_2_out));  // open: upper, rem
  Comparator #(.mode("unsigned"), .width(4)) comparator_9 (
    .a(ram_1_dout[15:12]), .b(in_6), .lt(comparator_9_lt));  // open: gt, eq
  Comparator #(.mode("unsigned"), .width(4)) comparator_10 (
    .a(ram_1_dout[15:12]), .b(in_15), .eq(comparator_10_eq));  // open: gt, lt
  Comparator #(.mode("unsigned"), .width(4)) comparator_11 (
    .a(ram_1_dout[15:12]), .b(in_16), .eq(comparator_11_eq));  // open: gt, lt
  Multiplexer #(.width(16)) multiplexer_14 (
    .in0(multiplexer_6_out), .in1(multiplexer_7_out), .out(multiplexer_14_out), .sel(or_2_out));
  Comparator #(.width(4)) comparator_12 (.a(ram_1_dout[15:12]), .b(in_20), .eq(comparator_12_eq));  // open: gt, lt
  or or_2 (or_2_out, comparator_10_eq, comparator_11_eq, comparator_8_eq);
  Multiplexer #(.select(3), .width(16)) multiplexer_15 (
    .in0(adder_4_out), .in1(adder_5_out), .in2(subtractor_5_out), .in3(subtractor_6_out),
    .in4(multiplier_1_out), .in5(multiplier_2_out), .in6(divider_1_out), .in7(divider_2_out),
    .out(multiplexer_15_out), .sel(subtractor_4_out[2:0]));
  Multiplexer #(.width(4)) multiplexer_16 (.in0(in_5), .in1(in_7), .out(multiplexer_16_out), .sel(comparator_9_lt));
  Adder #(.width(16)) adder_6 (.a(multiplexer_14_out), .b(bit_extender_4_out), .out(adder_6_out));  // open: cin, cout
  Comparator #(.mode("unsigned"), .width(4)) comparator_13 (
    .a(ram_1_dout[15:12]), .b(in_8), .lt(comparator_13_lt));  // open: gt, eq
  Multiplexer #(.width(4)) multiplexer_17 (
    .in0(multiplexer_16_out), .in1(in_9), .out(multiplexer_17_out), .sel(comparator_13_lt));
  Comparator #(.mode("unsigned"), .width(4)) comparator_14 (
    .a(ram_1_dout[15:12]), .b(in_10), .lt(comparator_14_lt));  // open: gt, eq
  Multiplexer #(.width(4)) multiplexer_18 (
    .in0(multiplexer_17_out), .in1(in_11), .out({multiplexer_18_out_2, multiplexer_18_out}),
    .sel(comparator_14_lt));

  // Notes on the sheet:
  //   in_21: initial=0xb
  //   in_13: initial=0x1
  //   in_23: initial=0x8
  //   in_12: initial=0x1
  //   in_19: initial=0xa
  //   in_2: initial=0xf
  //   in_17: initial=0xc
  //   in_18: initial=0x1
  //   in_20: initial=0xc
  //   in_16: initial=0xe
  //   in_15: initial=0xf
  //   in_6: initial=0xe
  //   in_5: initial=0x3
  //   in_7: initial=0x2
  //   in_8: initial=0xd
  //   in_9: initial=0x1
  //   in_10: initial=0x1
  //   Arnav Marchareddy
  //   CPU Name: Shuduck 2000
  //   I pledge my honor that I have abided by the Stevens Honor System
endmodule
